# Fritzing sketch Testaufbau (saved by Fritzing 0.9.3b)
breadboards: 1

parts:
  U1 = NodeMCU V1.0
  R1 = Resistor [tolerance=±5% resistance=330 package=THT]
  R2 = Resistor [tolerance=±5% resistance=330 package=THT]
  LED1 = LED - 5mm [color="Red (633nm)" package="5 mm [THT]"]
  LED2 = LED - 5mm [color="Blue (430nm)" package="5 mm [THT]"]
  S1 = Pushbutton [package="[THT]"]
  S2 = Pushbutton [package="[THT]"]
  R3 = Resistor [tolerance=±5% resistance=10k package=THT]
  R4 = Resistor [tolerance=±5% resistance=10k package=THT]
  DS1 = DS18B20 1-Wire Temperature Sensor [part_number=DS18B20]
  R5 = Resistor [tolerance=±5% resistance=220 package=THT]

nets:
  N1: U1.D1, S1.Pin_1, S1.Pin_2, R4.Pin_0
  N2: U1.D2, S2.Pin_1, S2.Pin_2, R3.Pin_0
  N3: U1.D3, DS1.DQ, R5.Pin_0
  3V3: U1.3V3, S1.Pin_3, S1.Pin_4, S2.Pin_3, S2.Pin_4, DS1.VDD, R5.Pin_1
  GND: U1.GND, LED1.anode, LED2.anode, R3.Pin_1, R4.Pin_1, DS1.GND
  N4: U1.D5, R2.Pin_1
  N5: U1.D6, R1.Pin_1
  N6: R1.Pin_0, LED2.cathode
  N7: R2.Pin_0, LED1.cathode

custom parts:
  NodeMCU V1.0: ESP8266 based NodeMCU
