# Fritzing sketch Testaufbau_LCD (saved by Fritzing 0.9.3b)
breadboards: 1

parts:
  U1 = NodeMCU V1.0
  U2 = Nokia 6100 Color LCD [package=nokia6100_lcd]

nets:
  N1: U1.D2, U2.DIO
  N2: U1.D3, U2.RESET
  N3: U1.3V3, U2.SCK
  N4: U1.GND, U2.CS

custom parts:
  NodeMCU V1.0: ESP8266 based NodeMCU
