# Fritzing sketch Testaufbau_LEDMatrix (saved by Fritzing 0.9.3b)
breadboards: 1

parts:
  U1 = NodeMCU V1.0
  LED1 = LED - 5mm [color="Red (633nm)" package="5 mm [THT]"]
  LED2 = LED - 5mm [color="Blue (430nm)" package="5 mm [THT]"]
  S1 = Pushbutton [package="[THT]"]
  S2 = Pushbutton [package="[THT]"]
  R3 = Resistor [tolerance=±5% resistance=10k package=THT]
  R4 = Resistor [tolerance=±5% resistance=10k package=THT]
  U2 = Mini-USB _B_ connector with 5th pin broken out. [package=usb-minib]
  U3 = Mini-USB _B_ connector with 5th pin broken out. [package=usb-minib]

nets:
  N1: U1.D1, S1.Pin_1, S1.Pin_2, R4.Pin_0
  N2: U1.D2, S2.Pin_1, S2.Pin_2, R3.Pin_0
  N3: U1.D4, U2.MTN4
  N4: U1.3V3, S1.Pin_3, S1.Pin_4, S2.Pin_3, S2.Pin_4, U2.MTN2, U3.MTN2
  N5: U1.GND, LED1.anode, LED2.anode, R3.Pin_1, R4.Pin_1, U2.MTN3, U3.MTN3
  N6: U1.D5, U2.D+, U3.D+
  N7: U1.D7, U2.MTN1, U3.MTN1
  N8: U1.D8, U3.MTN4

custom parts:
  NodeMCU V1.0: ESP8266 based NodeMCU
