# Fritzing sketch Testaufbau_nur_LED (saved by Fritzing 0.9.3b)
breadboards: 1

parts:
  U1 = NodeMCU V1.0
  R2 = Resistor [tolerance=±5% resistance=330 package=THT]
  LED1 = LED - 5mm [color="Red (633nm)" package="5 mm [THT]"]

nets:
  N1: U1.GND, LED1.anode
  N2: U1.D5, R2.Pin_1
  N3: R2.Pin_0, LED1.cathode

custom parts:
  NodeMCU V1.0: ESP8266 based NodeMCU
