# Fritzing sketch Testaufbau_zwei_LED (saved by Fritzing 0.9.3b)
breadboards: 1

parts:
  U1 = NodeMCU V1.0
  R1 = Resistor [tolerance=±5% resistance=330 package=THT]
  R2 = Resistor [tolerance=±5% resistance=330 package=THT]
  LED1 = LED - 5mm [color="Red (633nm)" package="5 mm [THT]"]
  LED2 = LED - 5mm [color="Blue (430nm)" package="5 mm [THT]"]

nets:
  N1: U1.GND, LED1.anode, LED2.anode
  N2: U1.D5, R2.Pin_1
  N3: U1.D6, R1.Pin_1
  N4: R1.Pin_0, LED2.cathode
  N5: R2.Pin_0, LED1.cathode

custom parts:
  NodeMCU V1.0: ESP8266 based NodeMCU
